// Digital circuit CG-16-1-Processor.dig as structural Verilog
module CG_16_1_Processor (
  input  clk,
  input  in_2,
  input  in_3,
  input  [7:0] in_4
);

  wire aawrite, aluread, aluwriteflags, and_1_out, and_4_out, and_5_out, and_6_out, and_7_out, and_8_out,
       and_9_out, aread, awrite, bsread, bswrite, carry, carryclear, carryset, ccclr, clock, comparator_1_eq,
       comparator_2_gt, comparator_3_eq, condjumpddesired, disableinterrupts, driver_13_out,
       enableinterrupts, equalclear, equalset, Fetch_Check_2_lt, Fetch_Check_eq, flagsread, flagswrite,
       Gr_RAM_check_eq, haltclock, interruptclear, interruptset, intread, intwrite, irread, irwrite,
       lessthanclear, lessthanset, mmuread, mmuwrite, morethanclear, morethanset, multiplexer_4_out,
       negativeclear, negativeset, or_1_out, or_3_out, Page_Select_q, pageclear, pageset, pcaddrsel,
       pcbsread, pcbswrite, pcclr, pcinc, pcread, pcseljump, pcwrite, Program_Counter_ovf, ROM_check_eq,
       sbread, sbwrite, stdec, stinc, stread, stwrite, telnet_1_av, telnet_1_out, xread, xwrite, yread,
       ywrite, zread, zwrite;
  wire [0:0] and_2_out, or_2_out;
  wire [2:0] condjump;
  wire [3:0] Control_Counter_out;
  wire [4:0] aluop;
  wire [6:2] flags;
  wire [7:0] address_bank, bsraddress_bank, pcaddress_bus;
  wire [11:0] aluflags;
  wire [11:1] busflags;
  wire [15:0] aaraddress, accumulator, address, blockramdualport_1_d, bus, cg_16_1_alu_1_x,
       cg_16_1_alu_1_x_high, instruction, interrupt, multiplexer_1_out, multiplexer_8_out, pcaddress,
       Stack_Base_Pointer_q, Stack_Top_Pointer_out, x, X_q, Y_q, Z_q;
  wire [50:11] multiplexer_7_out;
  wire [63:0] Control_ROM_d, multiplexer_5_out, multiplexer_6_out;

  Telnet #(.port(7000)) telnet_1 (.in(in_4), .C(clock), .wr(in_2), .rd(in_3), .out(telnet_1_out), .av(telnet_1_av));
  Multiplexer #(.Bits(16)) multiplexer_1 (.sel(aluread), .in_0(bus), .in_1(x), .out(multiplexer_1_out));
  or or_1 (or_1_out, stdec, stinc);
  assign clock = ~haltclock ? clk : 1'bz;  // DriverInvSel driverinvsel_1
  Register #(.Bits(16)) u_X (.D(bus), .C(clock), .en(xwrite), .Q(X_q));
  Register #(.Bits(16)) Y (.D(bus), .C(clock), .en(ywrite), .Q(Y_q));
  Register #(.Bits(16)) Z (.D(bus), .C(clock), .en(zwrite), .Q(Z_q));
  Register #(.Bits(16)) u_Accumulator (.D(multiplexer_1_out), .C(clock), .en(awrite), .Q(accumulator));
  CounterPreset #(.Bits(16)) Program_Counter (
    .en(pcinc), .C(clock), .dir(1'b0), .in(bus), .ld(pcwrite), .clr(pcclr), .out(pcaddress),
    .ovf(Program_Counter_ovf));
  Register #(.Bits(16)) Instruction_Register (.D(bus), .C(clock), .en(irwrite), .Q(instruction));
  CounterPreset #(.Bits(16)) Stack_Top_Pointer (
    .en(or_1_out), .C(clock), .dir(stdec), .in(bus), .ld(stwrite), .clr(1'b0), .out(Stack_Top_Pointer_out));  // open: ovf
  Register #(.Bits(16)) Stack_Base_Pointer (.D(bus), .C(clock), .en(sbwrite), .Q(Stack_Base_Pointer_q));
  Register #(.Bits(8)) Bank_Select_Register (.D(bus[7:0]), .C(clock), .en(bswrite), .Q(bsraddress_bank));
  Register #(.Bits(16)) Address_Access_Register (.D(bus), .C(clock), .en(aawrite), .Q(aaraddress));
  Register #(.Bits(16)) Interrupt_Register (.D(bus), .C(clock), .en(intwrite), .Q(interrupt));
  assign bus = xread ? X_q : 16'bz;  // Driver driver_1
  assign bus = yread ? Y_q : 16'bz;  // Driver driver_2
  assign bus = zread ? Z_q : 16'bz;  // Driver driver_3
  assign bus = aread ? accumulator : 16'bz;  // Driver driver_4
  assign bus = pcread ? pcaddress : 16'bz;  // Driver driver_5
  CounterPreset #(.Bits(8)) Program_Counter_Bank_Select (
    .en(Program_Counter_ovf), .C(clock), .dir(1'b0), .in(bus[7:0]), .ld(pcbswrite), .clr(pcclr),
    .out(pcaddress_bus));  // open: ovf
  assign bus = irread ? instruction : 16'bz;  // Driver driver_6
  assign bus = stread ? Stack_Top_Pointer_out : 16'bz;  // Driver driver_7
  assign bus = sbread ? Stack_Base_Pointer_q : 16'bz;  // Driver driver_8
  assign bus = intread ? interrupt : 16'bz;  // Driver driver_9
  assign bus = bsread ? {{8{1'b0}}, bsraddress_bank} : 16'bz;  // Driver driver_10
  assign bus = pcbsread ? {{8{1'b0}}, pcaddress_bus} : 16'bz;  // Driver driver_11
  Multiplexer #(.Bits(8)) multiplexer_2 (
    .sel(pcaddrsel), .in_0(bsraddress_bank), .in_1(pcaddress_bus), .out(address_bank));
  Multiplexer #(.Bits(16)) multiplexer_3 (.sel(pcaddrsel), .in_0(aaraddress), .in_1(pcaddress), .out(address));
  Counter #(.Bits(4)) Control_Counter (.en(~clock), .C(~clock), .clr(ccclr), .out(Control_Counter_out));  // open: ovf
  RS_FF Carry_Flag (.S(carryset), .C(clock), .R(carryclear), .Q(carry));  // open: nQ
  RS_FF Interrupt_Flag (.S(interruptset), .C(clock), .R(interruptclear), .Q(aluflags[2]));  // open: nQ
  RS_FF Negative_Flag (.S(negativeset), .C(clock), .R(negativeclear), .Q(flags[2]));  // open: nQ
  RS_FF More_Than_Flag (.S(morethanset), .C(clock), .R(morethanclear), .Q(flags[3]));  // open: nQ
  RS_FF Equal_Flag (.S(equalset), .C(clock), .R(equalclear), .Q(flags[4]));  // open: nQ
  RS_FF Less_Than_Flag (.S(lessthanset), .C(clock), .R(lessthanclear), .Q(flags[5]));  // open: nQ
  RS_FF Interrupt_Disable_Flag (.S(disableinterrupts), .C(clock), .R(enableinterrupts), .Q(flags[6]));  // open: nQ
  Multiplexer #(.Selector_Bits(3)) multiplexer_4 (
    .sel(condjump), .in_0(1'b0), .in_1(carry), .in_2(aluflags[2]), .in_3(flags[2]), .in_4(flags[3]),
    .in_5(flags[4]), .in_6(flags[5]), .in_7(flags[6]), .out(multiplexer_4_out));
  assign bus = flagsread ? {{9{1'b0}}, flags, aluflags[2], carry} : 16'bz;  // Driver driver_12
  Comparator #(.Bits(4)) Fetch_Check (.a(4'b0001), .b(Control_Counter_out), .eq(Fetch_Check_eq));  // open: gt, lt
  Comparator comparator_1 (.a(multiplexer_4_out), .b(condjumpddesired), .eq(comparator_1_eq));  // open: gt, lt
  LED u_Carry (.in(carry));
  LED u_Interrupt (.in(aluflags[2]));
  LED Negative (.in(flags[2]));
  LED More_Than (.in(flags[3]));
  LED Equal (.in(flags[4]));
  LED Less_Than (.in(flags[5]));
  LED Interrupt_Disable (.in(flags[6]));
  and and_1 (and_1_out, clock, Fetch_Check_eq);
  Comparator #(.Bits(4)) Fetch_Check_2 (.a(Control_Counter_out), .b(4'b0010), .lt(Fetch_Check_2_lt));  // open: gt, eq
  ROM #(.AddrBits(20), .Bits(64)) Control_ROM (.A({instruction, Control_Counter_out}), .sel(1'b1), .D(Control_ROM_d));
  Multiplexer #(.Bits(64)) multiplexer_5 (
    .sel(Control_Counter_out[0]), .in_0({64{1'b0}}), .in_1(64'h40000000040001), .out(multiplexer_5_out));
  Multiplexer #(.Bits(64)) multiplexer_6 (
    .sel(Control_Counter_out[0]), .in_0(64'h800), .in_1(64'h800040000), .out(multiplexer_6_out));
  Comparator #(.Bits(3)) comparator_2 (.a(condjump), .b(3'b000), .gt(comparator_2_gt));  // open: eq, lt
  assign driver_13_out = comparator_2_gt ? comparator_1_eq : 1'bz;  // Driver driver_13
  assign bus = and_2_out[0] ? multiplexer_8_out : 16'bz;  // Driver driver_14
  Demultiplexer demultiplexer_1 (.sel(pcseljump), .in(driver_13_out), .out_0(pcbswrite), .out_1(pcwrite));
  or or_2 (or_2_out[0], and_1_out, Fetch_Check_2_lt);
  Multiplexer #(.Selector_Bits(2), .Bits(64)) multiplexer_7 (
    .sel({aluflags[2], or_2_out[0]}), .in_0(Control_ROM_d), .in_1(multiplexer_5_out), .in_2(Control_ROM_d),
    .in_3(multiplexer_6_out),
    .out({intwrite, intread, pageclear, pageset, haltclock, condjumpddesired, condjump, pcaddrsel, aluread, stdec, stinc, multiplexer_7_out[50:49], flagswrite, flagsread, ccclr, enableinterrupts, disableinterrupts, multiplexer_7_out[43:32], aluwriteflags, aluop, aawrite, bswrite, bsread, sbwrite, sbread, stwrite, stread, irwrite, irread, pcseljump, pcbswrite, pcbsread, pcclr, pcinc, multiplexer_7_out[11], pcread, awrite, aread, zwrite, zread, ywrite, yread, xwrite, xread, mmuwrite, mmuread}));
  and and_2 (and_2_out[0], aluflags[2], ~clock);  // And
  Multiplexer #(.Selector_Bits(2), .Bits(16)) multiplexer_8 (
    .sel({Control_Counter_out[0], and_2_out[0]}), .in_0({16{1'b0}}), .in_1({16{1'b1}}), .in_2({16{1'b0}}),
    .in_3({16{1'b0}}), .out(multiplexer_8_out));
  and and_3 (pcinc, pcwrite, ~comparator_2_gt);  // And
  CG_16_1_ALU cg_16_1_alu_1 (
    .OP(aluop), .A(accumulator), .B(bus), .C_in(carry), .C_out(aluflags[0]), .N(aluflags[4]),
    .A_gt_B(aluflags[6]), .A_eq_B(aluflags[8]), .A_lt_B(aluflags[10]), .X(cg_16_1_alu_1_x),
    .X_high(cg_16_1_alu_1_x_high));  // open: Z
  Comparator #(.Bits(8)) Gr_RAM_check (.a(address_bank), .b({8{1'b1}}), .eq(Gr_RAM_check_eq));  // open: gt, lt
  Comparator #(.Bits(8)) ROM_check (.a(address_bank), .b({8{1'b0}}), .eq(ROM_check_eq));  // open: gt, lt
  and and_4 (and_4_out, Gr_RAM_check_eq, mmuread);
  Comparator #(.Bits(3)) comparator_3 (.a(condjump), .b(3'b000), .eq(comparator_3_eq));  // open: gt, lt
  assign pcwrite = comparator_3_eq ? multiplexer_7_out[11] : 1'bz;  // Driver driver_15
  Multiplexer #(.Bits(16)) multiplexer_9 (.sel(1'b0), .in_0(cg_16_1_alu_1_x), .in_1(cg_16_1_alu_1_x_high), .out(x));
  Multiplexer #(.Selector_Bits(2), .Bits(12)) multiplexer_10 (
    .sel({flagswrite, aluwriteflags}), .in_0(multiplexer_7_out[43:32]), .in_1(aluflags),
    .in_2({busflags[11], bus[5], busflags[9], bus[4], busflags[7], bus[3], busflags[5], bus[2], busflags[3], bus[1], busflags[1], bus[0]}),
    .in_3({12{1'b1}}),
    .out({lessthanclear, lessthanset, equalclear, equalset, morethanclear, morethanset, negativeclear, negativeset, interruptclear, interruptset, carryclear, carryset}));
  or or_3 (or_3_out, Gr_RAM_check_eq, ROM_check_eq);
  and and_5 (and_5_out, ROM_check_eq, mmuwrite);
  and and_6 (and_6_out, ROM_check_eq, mmuread);
  and and_7 (and_7_out, ~Gr_RAM_check_eq, mmuwrite);  // And
  and and_8 (and_8_out, mmuwrite, Gr_RAM_check_eq);
  RS_FF Page_Select (.S(pageset), .C(clock), .R(pageclear), .Q(Page_Select_q));  // open: nQ
  Stop Write_to_ROM_error (.stop(and_5_out));
  ROM #(.AddrBits(16), .isProgramMemory("true"), .Bits(16)) rom_1 (.A(address), .sel(and_6_out), .D(bus));
  BlockRAMDualPort #(.AddrBits(24), .Bits(16)) blockramdualport_1 (
    .A({address_bank, address}), .Din(bus), .str(and_7_out), .C(clock), .D(blockramdualport_1_d));
  GraphicCard #(.graphicHeight(160), .graphicWidth(200), .Bits(16)) graphiccard_1 (
    .A(address), .str(and_8_out), .C(clock), .ld(and_4_out), .B(Page_Select_q), .D(bus));
  not not_1 (aluflags[1], aluflags[0]);
  not not_2 (aluflags[3], aluflags[2]);
  not not_3 (aluflags[5], aluflags[4]);
  not not_4 (aluflags[7], aluflags[6]);
  not not_5 (aluflags[9], aluflags[8]);
  not not_6 (aluflags[11], aluflags[10]);
  assign bus = multiplexer_7_out[49] ? {{8{1'b0}}, instruction[7:0]} : 16'bz;  // Driver driver_16
  assign bus = multiplexer_7_out[50] ? {{8{1'b0}}, instruction[15:8]} : 16'bz;  // Driver driver_17
  and and_9 (and_9_out, mmuread, ~or_3_out);  // And
  assign bus = and_9_out ? blockramdualport_1_d : 16'bz;  // Driver driver_18
  not not_7 (busflags[1], bus[0]);
  not not_8 (busflags[3], bus[1]);
  not not_9 (busflags[5], bus[2]);
  not not_10 (busflags[7], bus[3]);
  not not_11 (busflags[9], bus[4]);
  not not_12 (busflags[11], bus[5]);

  // Other names for the same wires on the sheet: busflags (some bits) = bus[5:0]; flags[1:0] = {aluflags[2], carry};
  //   interruptflag = aluflags[2]

  // Notes on the sheet:
  //   clk: Hz: 5
  //   Registers
  //   Address Selection
  //   Flags
  //   Control Logic
  //   Fetch
  //   Conditional Jumps
  //   Interrupt Fetch
  //   contents of Control_ROM (hex, n*v repeats v):
  //   0,0,400000001000,15*0,1000,40400000001201,14*0,4000001001000,40000002000001
  //   ,400000001201,13*0,4000001001000,2000400,2000001,400000001009
  //   ,12*0,4000001001000,2000400,2000001,400000001021,12*0,4000001001000
  //   ,2000400,2000001,400000001081,12*0,4000001001000,2000400,2000001
  //   ,400000501001,12*0,4000001001000,2000400,2000001,400000001102
  //   ,12*0,4000001001000,2000400,2000001,400000001006,12*0,4000001001000
  //   ,2000400,2000001,400000001012,12*0,4000001001000,2000400,2000001
  //   ,400000001042,12*0,4000001001000,2000400,2000001,4000400000001002
  //   ,12*0,400000001108,15*0,400000001120,15*0,400000001180,15*0,400000001210
  //   ,15*0,400000001210,15*0,400000001240,15*0,400000801200,15*0,400000081008
  //   ,15*0,400000101004,15*0,400000201008,15*0,400000401004,15*0,8000002080000
  //   ,400000001102,14*0,8000002080000,c00000001002,14*0,10000002080000
  //   ,400000001201,14*0,10000002080000,1400000001001,14*0,4000001001000
  //   ,2000400,2000001,20400020001201,12*0,4000001001000,2000400,2000001
  //   ,20400024001201,12*0,4000001001000,2000400,2000001,20400028001201
  //   ,12*0,4000001001000,2000400,2000001,20400000001201,12*0,4000001001000
  //   ,2000400,2000001,20400004001201,12*0,4000001001000,2000400,2000001
  //   ,20400010001201,12*0,4000001001000,2000400,2000001,20400014001201
  //   ,12*0,4000001001000,2000400,2000001,20400018001201,12*0,4000001001000
  //   ,2000400,2000001,2040001c001201,12*0,4000001001000,2000400,2000001
  //   ,20000008000201,400000001102,11*0,20400008001200,15*0,204,20000008000200
  //   ,400000001108,13*0,210,20000008000200,400000001120,13*0,240,20000008000200
  //   ,400000001180,13*0,4000001001000,2000400,2000001,2000000c000201
  //   ,400000001102,11*0,2040000c001200,15*0,204,2000000c000200,400000001108
  //   ,13*0,210,2000000c000200,400000001120,13*0,240,2000000c000200
  //   ,400000001180,13*0,2040002c001200,15*0,20400030001200,15*0,20400034001200
  //   ,15*0,20400038001200,15*0,2040003c001200,15*0,20400040001200,15*0
  //   ,4000001001000,2000400,2000001,400080001001,12*0,4000001001000
  //   ,2000400,2000001,204,400080001001,11*0,4000001001000,2000400,2000001
  //   ,210,400080001001,11*0,4000001001000,2000400,2000001,240,400080001001
  //   ,11*0,4000001001000,2000400,2000001,808000,400000000801,11*0,8000002080000
  //   ,4002,8000002080000,402,4000001001000,2000400,2000001,400000001801
  //   ,8*0,10000002080000,801,10000002080000,8001,400000001000,11*0
  //   ,84400000000000,15*0,484400000000000,15*0,284400000000000,15*0
  //   ,684400000000000,15*0,704400000000000,15*0,604400000000000,15*0
  //   ,584400000000000,15*0,184400000000000,15*0,400200001000,15*0,400100001000
  //   ,15*0,600000001000,15*0,500000001000,15*0,2000400000001000,15*0
  //   ,1000400000001000,15*0,400800001000,15*0,800400000001000,15*0
  //   ,1000,8040400400000001
  //   MMU
  //   ALU
  //   microinstructions
  //   contents of rom_1 (hex, n*v repeats v):
  //   1,5eb,4
  //   Bus Flag Decoding
endmodule
